// Logisim project pcv1.circ as structural Verilog: 1 circuit, main circuit main
module main (
  input  Clock_Enable,
  input  in_2
);

  wire and_1_out, and_2_out, and_3_out, and_4_out, clock_1_out, dipswitch_1_sw1, dipswitch_1_sw2,
       dipswitch_1_sw3, dipswitch_1_sw4, j_k_ff_1_q, j_k_ff_1_qn, j_k_ff_2_q, j_k_ff_2_qn, j_k_ff_3_q,
       j_k_ff_3_qn, j_k_ff_4_qn, not_1_out;

  Clock clock_1 (.out(clock_1_out));
  J_K_Flip_Flop j_k_ff_1 (
    .J(Clock_Enable), .K(Clock_Enable), .clk(clock_1_out), .Q(j_k_ff_1_q), .Qn(j_k_ff_1_qn),
    .preset(and_4_out), .reset(not_1_out));
  J_K_Flip_Flop j_k_ff_2 (
    .J(Clock_Enable), .K(Clock_Enable), .clk(j_k_ff_1_q), .Q(j_k_ff_2_q), .Qn(j_k_ff_2_qn), .preset(and_3_out));  // open: reset
  J_K_Flip_Flop j_k_ff_3 (
    .J(Clock_Enable), .K(Clock_Enable), .clk(j_k_ff_2_q), .Q(j_k_ff_3_q), .Qn(j_k_ff_3_qn), .preset(and_2_out));  // open: reset
  J_K_Flip_Flop j_k_ff_4 (
    .J(Clock_Enable), .K(Clock_Enable), .clk(j_k_ff_3_q), .Qn(j_k_ff_4_qn), .preset(and_1_out));  // open: Q, reset
  not not_1 (not_1_out, and_4_out);
  LED led_1 (.in(j_k_ff_1_qn));
  LED led_2 (.in(j_k_ff_2_qn));
  LED led_3 (.in(j_k_ff_3_qn));
  LED led_4 (.in(j_k_ff_4_qn));
  and and_1 (and_1_out, in_2, dipswitch_1_sw1);
  DipSwitch dipswitch_1 (
    .sw1(dipswitch_1_sw1), .sw2(dipswitch_1_sw2), .sw3(dipswitch_1_sw3), .sw4(dipswitch_1_sw4));  // open: sw5, sw6, sw7, sw8
  and and_2 (and_2_out, dipswitch_1_sw2, in_2);
  and and_3 (and_3_out, dipswitch_1_sw3, in_2);
  and and_4 (and_4_out, dipswitch_1_sw4, in_2);

  // Notes on the sheet:
  //   Clock
endmodule
